// Logisim project Control unit.circ as structural Verilog: 2 circuits, main circuit main
module main (
  input  [3:0] in_1,
  output RegDst,
  output RegWrite,
  output ALU_SRC,
  output Mem_Read,
  output Mem_Write,
  output MemToReg,
  output Branch,
  output [1:0] AlUOp
);

  wire not_1_out, not_2_out, not_3_out, not_4_out, not_5_out, not_6_out, not_7_out, not_8_out, not_9_out,
       not_10_out;

  not not_1 (not_1_out, in_1[3]);
  not not_2 (not_2_out, in_1[2]);
  not not_3 (not_3_out, in_1[1]);
  not not_4 (not_4_out, in_1[0]);
  and R_Type (AlUOp[1], not_1_out, not_2_out, not_3_out, not_4_out);
  not not_5 (not_5_out, in_1[2]);
  not not_6 (not_6_out, in_1[1]);
  not not_7 (not_7_out, in_1[2]);
  and lw (Mem_Read, in_1[3], not_7_out, not_6_out, in_1[0]);
  not not_8 (not_8_out, in_1[0]);
  not not_9 (not_9_out, in_1[3]);
  and sw (AlUOp[0], in_1[3], not_5_out, in_1[1], not_8_out);
  not not_10 (not_10_out, in_1[1]);
  and beq (Branch, not_9_out, in_1[2], not_10_out, in_1[0]);
  or or_1 (RegWrite, AlUOp[1], Mem_Read);
  or or_2 (ALU_SRC, Mem_Read, AlUOp[0]);

  assign Mem_Write = AlUOp[0];
  assign MemToReg = Mem_Read;
  assign RegDst = AlUOp[1];
endmodule

module test (
  input  [3:0] in_1
);

  main main_1 ();  // open: in_1, RegDst, RegWrite, ALU_SRC, Mem_Read, Mem_Write, MemToReg, Branch, AlUOp
endmodule
